# Fritzing sketch GPIO_2 (saved by Fritzing 0.9.3b)
circuit board: 6cm x 9cm

parts:
  J1 = Raspberry Pi Header 40pin [form="♂ (male)" package=THT]
  J2 = Screw terminal - 2 pins [package=THT]
  J3 = screw terminal, 3 pins
  J4 = Screw terminal - 2 pins [package=THT]
  J5 = Screw terminal - 2 pins [package=THT]
  J6 = screw terminal, 3 pins
  J7 = Screw terminal - 2 pins [package=THT]
  J8 = Screw terminal - 2 pins [package=THT]
  J9 = Screw terminal - 2 pins [package=THT]
  J10 = Screw terminal - 2 pins [package=THT]
  J11 = screw terminal, 3 pins
  J12 = Screw terminal - 2 pins [package=THT]
  J13 = screw terminal, 3 pins
  J15 = Screw terminal - 2 pins [package=THT]
  J14 = screw terminal, 2 pins

nets:
  N1: J1.GPIO2, J4.pin1
  N2: J1.GPIO3, J14.pin2
  N3: J1.GIPO4, J2.pin1
  N4: J1.GND, J2.pin2, J4.pin2, J7.pin2, J10.pin2, J12.pin2, J14.pin1
  N5: J1.GIPO17, J3.pin1
  N6: J1.GIPO27, J3.pin2
  N7: J1.GIPO22, J3.pin3
  N8: J1.GIPO10, J5.pin1
  N9: J1.GIPO9, J5.pin2
  N10: J1.GIPO11, J12.pin1
  N11: J1.GIPO5, J13.pin1
  N12: J1.GIPO6, J13.pin2
  N13: J1.GIPO13, J13.pin3
  N14: J1.GIPO19, J15.pin1
  N15: J1.GIPO26, J15.pin2
  N16: J1.GIPO21, J11.pin3
  N17: J1.GIPO20, J11.pin2
  N18: J1.GIPO16, J11.pin1
  N19: J1.GIPO12, J10.pin1
  N20: J1.ID_SC, J9.pin2
  N21: J1.GIPO7, J9.pin1
  N22: J1.GIPO25, J6.pin3
  N23: J1.GIPO24, J6.pin2
  N24: J1.GIPO23, J6.pin1
  N25: J1.GIPO18, J7.pin1
  N26: J1.GIPO15, J8.pin2
  N27: J1.GIPO14, J8.pin1

custom parts:
  Raspberry Pi Header 40pin: Raspberry Pi 40 pin header - for creating your own shields.
